// Digital circuit 02 Adders.dig as structural Verilog
module _02_Adders (
  input  in_1,
  input  in_2,
  input  in_4,
  input  in_5,
  input  in_9,
  input  in_10,
  input  in_11,
  input  in_15,
  input  in_16,
  input  in_17,
  input  in_21,
  input  in_22,
  input  in_23,
  input  in_25,
  input  in_26,
  input  in_28,
  input  in_29,
  input  in_31,
  input  in_32,
  input  in_34,
  input  in_35,
  input  in_37,
  input  in_38,
  input  in_40,
  input  in_41,
  input  in_43,
  input  in_44,
  input  in_46,
  input  in_47,
  input  in_49,
  input  in_50,
  input  in_52,
  input  in_53,
  input  in_55,
  input  in_56,
  input  in_58,
  input  in_59,
  input  in_61,
  input  in_62,
  input  in_64,
  input  in_65,
  input  in_67,
  input  in_68,
  input  in_70,
  input  in_71,
  input  in_73,
  input  in_75,
  input  in_77,
  input  in_79,
  input  in_81,
  input  in_83,
  input  in_85,
  input  in_87,
  input  in_89,
  input  in_91,
  input  in_93,
  input  in_95,
  input  in_97,
  input  in_99,
  input  in_101,
  input  in_103,
  output out_3,
  output out_6,
  output out_7,
  output out_8,
  output out_12,
  output out_13,
  output out_14,
  output out_18,
  output out_19,
  output out_20,
  output out_24,
  output out_27,
  output out_30,
  output out_33,
  output out_36,
  output out_39,
  output out_42,
  output out_45,
  output out_48,
  output out_51,
  output out_54,
  output out_57,
  output out_60,
  output out_63,
  output out_66,
  output out_69,
  output out_72,
  output out_74,
  output out_76,
  output out_78,
  output out_80,
  output out_82,
  output out_84,
  output out_86,
  output out_88,
  output out_90,
  output out_92,
  output out_94,
  output out_96,
  output out_98,
  output out_100,
  output out_102
);

  wire add_1_c_o, add_2_c_o, add_3_c_o, add_4_c_o, add_5_c_o, add_6_c_o, add_7_c_o, add_8_c_o, add_9_c_o,
       add_10_c_o, add_11_c_o, add_12_c_o, add_13_c_o, add_14_c_o, add_15_c_o, add_16_c_o, add_17_c_o,
       add_18_c_o, add_19_c_o, add_20_c_o, add_21_c_o, add_22_c_o, add_23_c_o, add_24_c_o, add_25_c_o,
       add_26_c_o, add_27_c_o, add_28_c_o, add_29_c_o, add_30_c_o, add_31_c_o, add_32_c_o, and_2_out,
       and_3_out, nand_1_out, nand_2_out, nand_3_out, nand_4_out, nand_5_out, nand_6_out, nand_7_out,
       nand_8_out, nand_9_out, nand_10_out, nand_11_out, nand_13_out, nand_14_out, nand_15_out, nand_16_out,
       nand_17_out, nand_18_out, nand_19_out, nand_20_out, nand_21_out, nand_22_out, nand_23_out,
       nand_24_out, nand_25_out, nand_26_out, nand_27_out, nand_28_out, nand_29_out, nand_30_out,
       nand_31_out, nand_34_out, nand_35_out, pulldown_1_out, pulldown_3_out, xor_2_out;

  nand nand_1 (nand_1_out, in_1, in_1);
  nand nand_2 (nand_2_out, in_2, in_2);
  nand nand_3 (nand_3_out, in_1, in_2);
  nand nand_4 (nand_4_out, in_9, in_9);
  nand nand_5 (nand_5_out, in_10, in_10);
  nand nand_6 (nand_6_out, in_9, in_10);
  nand nand_7 (nand_7_out, nand_31_out, nand_31_out);
  nand nand_8 (nand_8_out, in_11, in_11);
  nand nand_9 (nand_9_out, nand_31_out, in_11);
  Add add_1 (.a(in_25), .b(in_26), .c_i(pulldown_1_out), .s(out_24), .c_o(add_1_c_o));
  PullDown pulldown_1 (.out(pulldown_1_out));
  Add add_2 (.a(in_28), .b(in_29), .c_i(add_1_c_o), .s(out_27), .c_o(add_2_c_o));
  Add add_3 (.a(in_31), .b(in_32), .c_i(add_2_c_o), .s(out_30), .c_o(add_3_c_o));
  Add add_4 (.a(in_34), .b(in_35), .c_i(add_3_c_o), .s(out_33), .c_o(add_4_c_o));
  Add add_5 (.a(in_37), .b(in_38), .c_i(add_4_c_o), .s(out_36), .c_o(add_5_c_o));
  Add add_6 (.a(in_40), .b(in_41), .c_i(add_5_c_o), .s(out_39), .c_o(add_6_c_o));
  Add add_7 (.a(in_43), .b(in_44), .c_i(add_6_c_o), .s(out_42), .c_o(add_7_c_o));
  Add add_8 (.a(in_46), .b(in_47), .c_i(add_7_c_o), .s(out_45), .c_o(add_8_c_o));
  Add add_9 (.a(in_49), .b(in_50), .c_i(add_8_c_o), .s(out_48), .c_o(add_9_c_o));
  Add add_10 (.a(in_52), .b(in_53), .c_i(add_9_c_o), .s(out_51), .c_o(add_10_c_o));
  Add add_11 (.a(in_55), .b(in_56), .c_i(add_10_c_o), .s(out_54), .c_o(add_11_c_o));
  Add add_12 (.a(in_58), .b(in_59), .c_i(add_11_c_o), .s(out_57), .c_o(add_12_c_o));
  Add add_13 (.a(in_61), .b(in_62), .c_i(add_12_c_o), .s(out_60), .c_o(add_13_c_o));
  Add add_14 (.a(in_64), .b(in_65), .c_i(add_13_c_o), .s(out_63), .c_o(add_14_c_o));
  Add add_15 (.a(in_67), .b(in_68), .c_i(add_14_c_o), .s(out_66), .c_o(add_15_c_o));
  Add add_16 (.a(in_70), .b(in_71), .c_i(add_15_c_o), .s(out_69), .c_o(add_16_c_o));
  PullDown pulldown_2 (.out(add_16_c_o));
  nand nand_10 (nand_10_out, in_1, nand_2_out);
  nand nand_11 (nand_11_out, nand_1_out, in_2);
  nand nand_12 (out_8, nand_3_out, nand_3_out);
  nand nand_13 (nand_13_out, nand_6_out, nand_6_out);
  nand nand_14 (nand_14_out, nand_31_out, nand_8_out);
  nand nand_15 (nand_15_out, nand_7_out, in_11);
  nand nand_16 (nand_16_out, nand_9_out, nand_9_out);
  nand nand_17 (nand_17_out, in_9, nand_5_out);
  nand nand_18 (nand_18_out, nand_4_out, in_10);
  nand nand_19 (nand_19_out, nand_10_out, nand_10_out);
  nand nand_20 (nand_20_out, nand_11_out, nand_11_out);
  nand nand_21 (nand_21_out, nand_17_out, nand_17_out);
  nand nand_22 (nand_22_out, nand_18_out, nand_18_out);
  nand nand_23 (nand_23_out, nand_14_out, nand_14_out);
  nand nand_24 (nand_24_out, nand_15_out, nand_15_out);
  nand nand_25 (nand_25_out, nand_19_out, nand_19_out);
  nand nand_26 (nand_26_out, nand_20_out, nand_20_out);
  nand nand_27 (nand_27_out, nand_21_out, nand_21_out);
  nand nand_28 (nand_28_out, nand_22_out, nand_22_out);
  nand nand_29 (nand_29_out, nand_23_out, nand_23_out);
  nand nand_30 (nand_30_out, nand_24_out, nand_24_out);
  nand nand_31 (nand_31_out, nand_27_out, nand_28_out);
  nand nand_32 (out_12, nand_29_out, nand_30_out);
  nand nand_33 (out_3, nand_25_out, nand_26_out);
  nand nand_34 (nand_34_out, nand_13_out, nand_13_out);
  nand nand_35 (nand_35_out, nand_16_out, nand_16_out);
  Add add_17 (.a(in_73), .b(1'b1), .c_i(pulldown_3_out), .s(out_72), .c_o(add_17_c_o));
  PullDown pulldown_3 (.out(pulldown_3_out));
  Add add_18 (.a(in_75), .b(1'b0), .c_i(add_17_c_o), .s(out_74), .c_o(add_18_c_o));
  Add add_19 (.a(in_77), .b(1'b0), .c_i(add_18_c_o), .s(out_76), .c_o(add_19_c_o));
  Add add_20 (.a(in_79), .b(1'b0), .c_i(add_19_c_o), .s(out_78), .c_o(add_20_c_o));
  Add add_21 (.a(in_81), .b(1'b0), .c_i(add_20_c_o), .s(out_80), .c_o(add_21_c_o));
  Add add_22 (.a(in_83), .b(1'b0), .c_i(add_21_c_o), .s(out_82), .c_o(add_22_c_o));
  Add add_23 (.a(in_85), .b(1'b0), .c_i(add_22_c_o), .s(out_84), .c_o(add_23_c_o));
  Add add_24 (.a(in_87), .b(1'b0), .c_i(add_23_c_o), .s(out_86), .c_o(add_24_c_o));
  Add add_25 (.a(in_89), .b(1'b0), .c_i(add_24_c_o), .s(out_88), .c_o(add_25_c_o));
  Add add_26 (.a(in_91), .b(1'b0), .c_i(add_25_c_o), .s(out_90), .c_o(add_26_c_o));
  Add add_27 (.a(in_93), .b(1'b0), .c_i(add_26_c_o), .s(out_92), .c_o(add_27_c_o));
  Add add_28 (.a(in_95), .b(1'b0), .c_i(add_27_c_o), .s(out_94), .c_o(add_28_c_o));
  Add add_29 (.a(in_97), .b(1'b0), .c_i(add_28_c_o), .s(out_96), .c_o(add_29_c_o));
  Add add_30 (.a(in_99), .b(1'b0), .c_i(add_29_c_o), .s(out_98), .c_o(add_30_c_o));
  Add add_31 (.a(in_101), .b(1'b0), .c_i(add_30_c_o), .s(out_100), .c_o(add_31_c_o));
  Add add_32 (.a(in_103), .b(1'b0), .c_i(add_31_c_o), .s(out_102), .c_o(add_32_c_o));
  PullDown pulldown_4 (.out(add_32_c_o));
  nand nand_36 (out_13, nand_34_out, nand_35_out);
  xor xor_1 (out_6, in_4, in_5);
  and and_1 (out_7, in_4, in_5);
  xor xor_2 (xor_2_out, in_15, in_16);
  and and_2 (and_2_out, in_15, in_16);
  xor xor_3 (out_18, xor_2_out, in_17);
  and and_3 (and_3_out, xor_2_out, in_17);
  Add add_33 (.a(in_21), .b(in_22), .c_i(in_23), .s(out_19), .c_o(out_20));
  or or_1 (out_14, and_2_out, and_3_out);
endmodule
