// Digital circuit 1.LogicGates.dig as structural Verilog
module _1_LogicGates (
  input  in_1,
  input  in_2,
  input  in_4,
  input  in_8,
  input  in_9,
  input  in_10,
  input  in_11,
  input  in_13,
  input  in_14,
  input  in_15,
  input  in_16,
  input  in_19,
  input  in_20,
  input  in_21,
  input  in_22,
  input  in_24,
  input  in_25,
  input  in_27,
  input  in_28,
  input  in_30,
  input  in_32,
  input  in_33,
  input  in_35,
  input  in_36,
  input  in_37,
  input  in_38,
  input  in_40,
  input  in_41,
  input  in_42,
  input  in_43,
  input  in_45,
  input  in_47,
  input  in_49,
  input  in_50,
  input  in_55,
  input  in_56,
  input  in_58,
  output out_3,
  output out_5,
  output out_6,
  output out_7,
  output out_12,
  output out_17,
  output out_18,
  output out_23,
  output out_26,
  output out_29,
  output out_31,
  output out_34,
  output out_39,
  output out_44,
  output out_46,
  output out_48,
  output out_51,
  output out_52,
  output out_53,
  output out_54,
  output out_57
);

  wire and_1_out, and_2_out, and_3_out, and_4_out, nand_1_out, nand_2_out, nand_3_out, nand_4_out,
       nand_5_out, nand_6_out, nand_7_out, nand_8_out, nand_9_out, nand_10_out, nand_11_out, nand_12_out,
       nand_13_out, nand_14_out, nand_15_out, nand_16_out, nand_17_out, nand_18_out, nand_19_out,
       nand_20_out, nand_21_out, nand_22_out, not_1_out, not_2_out, not_3_out, not_4_out, not_5_out,
       not_6_out;

  nand nand_1 (nand_1_out, in_24, in_24);
  nand nand_2 (nand_2_out, in_25, in_25);
  nand nand_3 (nand_3_out, in_40, in_40);
  nand nand_4 (nand_4_out, in_24, nand_2_out);
  nand nand_5 (nand_5_out, nand_1_out, in_25);
  nand nand_6 (nand_6_out, in_37, nand_3_out);
  nand nand_7 (nand_7_out, in_38, in_40);
  nand nand_8 (nand_8_out, nand_4_out, nand_4_out);
  nand nand_9 (nand_9_out, nand_5_out, nand_5_out);
  nand nand_10 (nand_10_out, nand_6_out, nand_6_out);
  nand nand_11 (nand_11_out, nand_7_out, nand_7_out);
  not not_1 (not_1_out, in_30);
  not not_2 (not_2_out, in_32);
  nand nand_12 (nand_12_out, in_15, in_15);
  nand nand_13 (nand_13_out, in_16, in_16);
  not not_3 (not_3_out, in_36);
  nand nand_14 (nand_14_out, in_50, in_50);
  nand nand_15 (nand_15_out, in_10, in_11);
  nand nand_16 (nand_16_out, in_13, in_14);
  not not_4 (not_4_out, in_21);
  not not_5 (not_5_out, in_22);
  nand nand_17 (nand_17_out, nand_8_out, nand_8_out);
  nand nand_18 (nand_18_out, nand_9_out, nand_9_out);
  and and_1 (and_1_out, in_30, not_2_out);
  and and_2 (and_2_out, not_1_out, in_32);
  and and_3 (and_3_out, in_33, not_3_out);
  and and_4 (and_4_out, in_35, in_36);
  nand nand_19 (nand_19_out, nand_10_out, nand_10_out);
  nand nand_20 (nand_20_out, nand_11_out, nand_11_out);
  nand nand_21 (nand_21_out, in_49, nand_14_out);
  nand nand_22 (nand_22_out, in_49, in_50);
  not not_6 (not_6_out, in_47);
  nand nand_23 (out_6, in_4, in_4);
  nand nand_24 (out_12, nand_15_out, nand_15_out);
  nand nand_25 (out_17, nand_12_out, nand_13_out);
  nand nand_26 (out_23, not_4_out, not_5_out);
  nand nand_27 (out_26, nand_17_out, nand_18_out);
  or or_1 (out_31, and_1_out, and_2_out);
  or or_2 (out_34, and_3_out, and_4_out);
  nand nand_28 (out_39, nand_19_out, nand_20_out);
  nand nand_29 (out_51, nand_21_out, nand_21_out);
  nand nand_30 (out_52, nand_22_out, nand_22_out);
  and and_5 (out_48, in_45, not_6_out);
  and and_6 (out_46, in_45, in_47);
  not not_7 (out_3, nand_16_out);
  nand nand_31 (out_5, in_1, in_2);
  not not_8 (out_57, in_58);
  and and_7 (out_7, in_8, in_9);
  or or_3 (out_18, in_19, in_20);
  xor xor_1 (out_29, in_27, in_28);
  Multiplexer multiplexer_1 (.sel(in_41), .in_0(in_42), .in_1(in_43), .out(out_44));
  Demultiplexer demultiplexer_1 (.sel(in_56), .in(in_55), .out_0(out_53), .out_1(out_54));
endmodule
