// Digital circuit basic_gates.dig as structural Verilog
module basic_gates (
  input  in_1,
  input  in_2,
  input  in_4,
  input  in_8,
  input  in_9,
  input  in_10,
  input  in_11,
  input  in_13,
  input  in_14,
  input  in_16,
  input  in_17,
  input  in_18,
  input  in_21,
  input  in_22,
  input  in_23,
  input  in_24,
  input  in_26,
  input  in_27,
  input  in_29,
  input  in_30,
  input  in_32,
  input  in_34,
  input  in_35,
  input  in_37,
  input  in_38,
  input  in_39,
  input  in_40,
  input  in_42,
  input  in_43,
  input  in_44,
  input  in_45,
  input  in_47,
  input  in_49,
  input  in_51,
  input  in_52,
  input  in_57,
  input  in_58,
  output out_3,
  output out_5,
  output out_6,
  output out_7,
  output out_12,
  output out_15,
  output out_19,
  output out_20,
  output out_25,
  output out_28,
  output out_31,
  output out_33,
  output out_36,
  output out_41,
  output out_46,
  output out_48,
  output out_50,
  output out_53,
  output out_54,
  output out_55,
  output out_56
);

  wire and_1_out, and_2_out, and_3_out, and_4_out, nand_1_out, nand_2_out, nand_3_out, nand_4_out,
       nand_5_out, nand_6_out, nand_7_out, nand_8_out, nand_9_out, nand_10_out, nand_11_out, nand_12_out,
       nand_13_out, nand_14_out, nand_15_out, nand_16_out, nand_17_out, nand_18_out, nand_19_out,
       nand_20_out, nand_21_out, nand_22_out, not_1_out, not_2_out, not_3_out, not_4_out, not_5_out,
       not_6_out;

  nand nand_1 (nand_1_out, in_26, in_26);
  nand nand_2 (nand_2_out, in_27, in_27);
  nand nand_3 (nand_3_out, in_42, in_42);
  nand nand_4 (nand_4_out, in_26, nand_2_out);
  nand nand_5 (nand_5_out, nand_1_out, in_27);
  nand nand_6 (nand_6_out, in_39, nand_3_out);
  nand nand_7 (nand_7_out, in_40, in_42);
  nand nand_8 (nand_8_out, nand_4_out, nand_4_out);
  nand nand_9 (nand_9_out, nand_5_out, nand_5_out);
  nand nand_10 (nand_10_out, nand_6_out, nand_6_out);
  nand nand_11 (nand_11_out, nand_7_out, nand_7_out);
  not not_1 (not_1_out, in_32);
  not not_2 (not_2_out, in_34);
  nand nand_12 (nand_12_out, in_17, in_17);
  nand nand_13 (nand_13_out, in_18, in_18);
  nand nand_14 (nand_14_out, nand_8_out, nand_8_out);
  nand nand_15 (nand_15_out, nand_9_out, nand_9_out);
  not not_3 (not_3_out, in_38);
  nand nand_16 (nand_16_out, nand_10_out, nand_10_out);
  nand nand_17 (nand_17_out, nand_11_out, nand_11_out);
  nand nand_18 (nand_18_out, in_52, in_52);
  nand nand_19 (nand_19_out, in_10, in_11);
  nand nand_20 (nand_20_out, in_13, in_14);
  not not_4 (not_4_out, in_23);
  not not_5 (not_5_out, in_24);
  and and_1 (and_1_out, in_32, not_2_out);
  and and_2 (and_2_out, not_1_out, in_34);
  and and_3 (and_3_out, in_35, not_3_out);
  and and_4 (and_4_out, in_37, in_38);
  nand nand_21 (nand_21_out, in_51, nand_18_out);
  nand nand_22 (nand_22_out, in_51, in_52);
  not not_6 (not_6_out, in_49);
  nand nand_23 (out_5, in_1, in_2);
  nand nand_24 (out_6, in_4, in_4);
  nand nand_25 (out_12, nand_19_out, nand_19_out);
  nand nand_26 (out_19, nand_12_out, nand_13_out);
  nand nand_27 (out_25, not_4_out, not_5_out);
  nand nand_28 (out_28, nand_14_out, nand_15_out);
  or or_1 (out_33, and_1_out, and_2_out);
  or or_2 (out_36, and_3_out, and_4_out);
  nand nand_29 (out_41, nand_16_out, nand_17_out);
  nand nand_30 (out_53, nand_21_out, nand_21_out);
  nand nand_31 (out_54, nand_22_out, nand_22_out);
  and and_5 (out_50, in_47, not_6_out);
  and and_6 (out_48, in_47, in_49);
  not not_7 (out_3, nand_20_out);
  not not_8 (out_15, in_16);
  and and_7 (out_7, in_8, in_9);
  or or_3 (out_20, in_21, in_22);
  xor xor_1 (out_31, in_29, in_30);
  Multiplexer multiplexer_1 (.sel(in_43), .in_0(in_44), .in_1(in_45), .out(out_46));
  Demultiplexer demultiplexer_1 (.sel(in_58), .in(in_57), .out_0(out_55), .out_1(out_56));
endmodule
