// Logisim project components_diagrams.circ as structural Verilog: 1 circuit, main circuit main
module main (
);

  wire and_1_out, and_2_out, buffer_1_out, buffer_2_out, buffer_3_out, demultiplexer_1_out0,
       demultiplexer_1_out1, multiplexer_1_out, nand_1_out, nand_2_out, nand_3_out, nand_4_out, nand_5_out,
       nand_6_out, nor_1_out, not_1_out, not_2_out, or_1_out, or_2_out, undriven, undriven_2, undriven_3,
       undriven_4, undriven_5, undriven_6, undriven_7, undriven_8, undriven_9, undriven_10, undriven_11,
       undriven_12, undriven_13, undriven_14, undriven_15, undriven_16, undriven_17, undriven_18,
       undriven_19, undriven_20, undriven_21, undriven_22, undriven_23, undriven_24, undriven_25,
       undriven_26, undriven_27, undriven_28, undriven_29, undriven_30, undriven_31, xnor_1_out, xor_1_out;

  not not_1 (not_1_out, undriven);
  and and_1 (and_1_out, undriven_2, undriven_3);
  nand nand_1 (nand_1_out, undriven_4, undriven_5);
  xor xor_1 (xor_1_out, undriven_6, undriven_7);
  not not_2 (not_2_out, undriven_8);
  and and_2 (and_2_out, undriven_9, undriven_10);
  or or_1 (or_1_out, undriven_11, undriven_12);
  nand nand_2 (nand_2_out, undriven_13, undriven_14);
  Multiplexer multiplexer_1 (.in0(undriven_15), .in1(undriven_16), .out(multiplexer_1_out), .sel(undriven_18));
  Demultiplexer demultiplexer_1 (
    .out0(demultiplexer_1_out0), .out1(demultiplexer_1_out1), .in(undriven_17), .sel(undriven_19));
  buf buffer_1 (buffer_1_out, undriven_24);
  buf buffer_2 (buffer_2_out, undriven_22);
  buf buffer_3 (buffer_3_out, undriven_23);
  or or_2 (or_2_out, undriven_25, undriven_26);
  nor nor_1 (nor_1_out, undriven_27, undriven_28);
  xnor xnor_1 (xnor_1_out, undriven_29, undriven_30);
  nand nand_3 (nand_3_out, undriven_31, undriven_31);
  nand nand_4 (nand_4_out, undriven_20, undriven_21);
  nand nand_5 (nand_5_out, buffer_2_out, buffer_3_out);
  nand nand_6 (nand_6_out, nand_4_out, nand_4_out);

  // Notes on the sheet:
  //   NOT
  //   in
  //   AND
  //   a
  //   b
  //   NAND
  //   a
  //   b
  //   XOR
  //   a
  //   b
  //   NOT
  //   in
  //   AND
  //   a
  //   b
  //   OR
  //   a
  //   b
  //   out
  //   out
  //   out
  //   out
  //   a
  //   b
  //   out
  //   out
  //   out
  //   NAND
  //   in
  //   a
  //   b
  //   a
  //   b
  //   a
  //   b
  //   sel
  //   in
  //   sel
  //   Buffer
  //   in
  //   OR
  //   a
  //   b
  //   NOR
  //   a
  //   b
  //   XNOR
  //   a
  //   b
  //   out
  //   MULTIPLEXER
  //   out
  //   DEMULTIPLEXER
  //   a
  //   b
  //   out
  //   out
  //   out
  //   out
  //   out
  //   out
  //   out
endmodule
