// Logisim project gates_diagrams.circ as structural Verilog: 1 circuit, main circuit main
module main (
);

  wire and_1_out, and_2_out, and_3_out, and_4_out, and_5_out, and_6_out, and_7_out, and_8_out, and_9_out,
       and_10_out, and_11_out, and_12_out, and_13_out, and_14_out, and_15_out, and_16_out, and_17_out,
       and_18_out, and_19_out, and_20_out, and_21_out, and_22_out, and_23_out, buffer_1_out, buffer_2_out,
       demultiplexer_1_out0, demultiplexer_1_out1, demultiplexer_2_out0, demultiplexer_2_out1,
       demultiplexer_3_out0, demultiplexer_3_out1, demultiplexer_4_out0, demultiplexer_4_out1,
       demultiplexer_5_out0, demultiplexer_5_out1, demultiplexer_6_out0, demultiplexer_6_out1,
       demultiplexer_7_out0, demultiplexer_7_out1, demultiplexer_8_out0, demultiplexer_8_out1,
       demultiplexer_9_out0, demultiplexer_9_out1, demultiplexer_10_out0, demultiplexer_10_out1,
       demultiplexer_11_out0, demultiplexer_11_out1, multiplexer_1_out, multiplexer_2_out, multiplexer_3_out,
       multiplexer_4_out, multiplexer_5_out, multiplexer_6_out, multiplexer_7_out, multiplexer_8_out,
       multiplexer_9_out, multiplexer_10_out, multiplexer_11_out, multiplexer_12_out, multiplexer_13_out,
       multiplexer_14_out, multiplexer_15_out, multiplexer_16_out, multiplexer_17_out, nand_1_out,
       nand_2_out, nand_3_out, nand_4_out, not_1_out, not_2_out, not_3_out, not_4_out, not_5_out, not_6_out,
       not_7_out, not_8_out, not_9_out, not_10_out, not_11_out, not_12_out, not_13_out, not_14_out,
       not_15_out, not_16_out, not_17_out, not_18_out, not_19_out, not_20_out, not_21_out, or_1_out,
       or_2_out, or_3_out, or_4_out, or_5_out, or_6_out, or_7_out, or_8_out, or_9_out, or_10_out, or_11_out,
       or_12_out, or_13_out, or_14_out, or_15_out, or_16_out, or_17_out, or_18_out, or_19_out, or_20_out,
       or_21_out, or_22_out, or_23_out, or_24_out, or_25_out, or_26_out, undriven, undriven_2, undriven_3,
       undriven_4, undriven_5, undriven_6, undriven_7, undriven_8, undriven_9, undriven_10, undriven_11,
       undriven_12, undriven_13, undriven_14, undriven_15, undriven_16, undriven_17, undriven_18,
       undriven_19, undriven_20, undriven_21, undriven_22, undriven_23, undriven_24, undriven_25,
       undriven_26, undriven_27, undriven_28, undriven_29, undriven_30, undriven_31, undriven_32,
       undriven_33, undriven_34, undriven_35, undriven_36, undriven_37, undriven_38, undriven_39,
       undriven_40, undriven_41, undriven_42, undriven_43, undriven_44, undriven_45, undriven_46,
       undriven_47, undriven_48, undriven_49, undriven_50, undriven_51, undriven_52, undriven_53,
       undriven_54, undriven_55, undriven_56, undriven_57, undriven_58, undriven_59, undriven_60,
       undriven_61, undriven_62, undriven_63, undriven_64, undriven_65, undriven_66, undriven_67,
       undriven_68, undriven_69, undriven_70, undriven_71, undriven_72, undriven_73, undriven_74,
       undriven_75, undriven_76, undriven_77, undriven_78, undriven_79, undriven_80, undriven_81,
       undriven_82, undriven_83, undriven_84, undriven_85, undriven_86, undriven_87, undriven_88,
       undriven_89, undriven_90, undriven_91, undriven_92, undriven_93, undriven_94, undriven_95,
       undriven_96, undriven_97, undriven_98, undriven_99, undriven_100, undriven_101, undriven_102,
       undriven_103, undriven_104, undriven_105, undriven_106, undriven_107, undriven_108, undriven_109,
       undriven_110, undriven_111, undriven_112, undriven_113, undriven_114, undriven_115, undriven_116,
       undriven_117, undriven_118, undriven_119, undriven_120, undriven_121, undriven_122, undriven_123,
       undriven_124, undriven_125, undriven_126, undriven_127, undriven_128, undriven_129, undriven_130,
       undriven_131, undriven_132, undriven_133, undriven_134, undriven_135, undriven_136, undriven_137,
       undriven_138, undriven_139, undriven_140, undriven_141, undriven_142, undriven_143, undriven_144,
       undriven_145, undriven_146, undriven_147, undriven_148, undriven_149, undriven_150, undriven_151,
       undriven_152, undriven_153, undriven_154, undriven_155, undriven_156, undriven_157, undriven_158,
       undriven_159, undriven_167, undriven_172, undriven_173, undriven_174, undriven_175, undriven_176,
       undriven_177, undriven_178, undriven_179, undriven_180, undriven_181, undriven_182, xor_1_out;
  wire [15:0] multiplexer_18_out, multiplexer_19_out, multiplexer_20_out, multiplexer_21_out,
       multiplexer_22_out, multiplexer_23_out, multiplexer_24_out, multiplexer_25_out, multiplexer_26_out,
       multiplexer_27_out, undriven_160, undriven_161, undriven_162, undriven_163, undriven_164,
       undriven_165, undriven_166, undriven_168, undriven_169, undriven_170, undriven_171;

  and and_1 (and_1_out, undriven, undriven_2);
  and and_2 (and_2_out, undriven_3, undriven_4);
  and and_3 (and_3_out, undriven_5, undriven_6);
  and and_4 (and_4_out, undriven_7, undriven_8);
  and and_5 (and_5_out, undriven_9, undriven_10);
  and and_6 (and_6_out, undriven_11, undriven_12);
  and and_7 (and_7_out, undriven_13, undriven_14);
  and and_8 (and_8_out, undriven_15, undriven_16);
  and and_9 (and_9_out, undriven_17, undriven_18);
  and and_10 (and_10_out, undriven_19, undriven_20);
  and and_11 (and_11_out, undriven_21, undriven_22);
  and and_12 (and_12_out, undriven_23, undriven_24);
  and and_13 (and_13_out, undriven_25, undriven_26);
  and and_14 (and_14_out, undriven_27, undriven_28);
  and and_15 (and_15_out, undriven_29, undriven_30);
  and and_16 (and_16_out, undriven_31, undriven_32);
  not not_1 (not_1_out, undriven_33);
  and and_17 (and_17_out, undriven_34, undriven_35);
  or or_1 (or_1_out, undriven_36, undriven_37);
  Multiplexer multiplexer_1 (.in0(undriven_40), .in1(undriven_41), .out(multiplexer_1_out), .sel(undriven_43));
  Demultiplexer demultiplexer_1 (
    .out0(demultiplexer_1_out0), .out1(demultiplexer_1_out1), .in(undriven_42));  // open: sel
  xor xor_1 (xor_1_out, undriven_38, undriven_39);
  nand nand_1 (nand_1_out, undriven_85, undriven_85);
  nand nand_2 (nand_2_out, undriven_47, undriven_48);
  buf buffer_1 (buffer_1_out, undriven_49);
  buf buffer_2 (buffer_2_out, undriven_50);
  not not_2 (not_2_out, undriven_44);
  not not_3 (not_3_out, undriven_45);
  not not_4 (not_4_out, undriven_87);
  not not_5 (not_5_out, undriven_86);
  or or_2 (or_2_out, undriven_53, undriven_54);
  or or_3 (or_3_out, undriven_55, undriven_56);
  or or_4 (or_4_out, undriven_57, undriven_58);
  or or_5 (or_5_out, undriven_59, undriven_60);
  or or_6 (or_6_out, undriven_61, undriven_62);
  or or_7 (or_7_out, undriven_63, undriven_64);
  or or_8 (or_8_out, undriven_65, undriven_66);
  or or_9 (or_9_out, undriven_67, undriven_68);
  or or_10 (or_10_out, undriven_69, undriven_70);
  or or_11 (or_11_out, undriven_71, undriven_72);
  or or_12 (or_12_out, undriven_73, undriven_74);
  or or_13 (or_13_out, undriven_75, undriven_76);
  or or_14 (or_14_out, undriven_77, undriven_78);
  or or_15 (or_15_out, undriven_79, undriven_80);
  or or_16 (or_16_out, undriven_81, undriven_82);
  or or_17 (or_17_out, undriven_83, undriven_84);
  nand nand_3 (nand_3_out, buffer_1_out, buffer_2_out);
  and and_18 (and_18_out, not_2_out, undriven_45);
  and and_19 (and_19_out, undriven_44, not_3_out);
  and and_20 (and_20_out, undriven_51, not_4_out);
  and and_21 (and_21_out, undriven_52, undriven_87);
  and and_22 (and_22_out, not_5_out, undriven_46);
  and and_23 (and_23_out, undriven_86, undriven_46);
  nand nand_4 (nand_4_out, nand_2_out, nand_2_out);
  or or_18 (or_18_out, and_18_out, and_19_out);
  or or_19 (or_19_out, and_20_out, and_21_out);
  not not_6 (not_6_out, undriven_88);
  not not_7 (not_7_out, undriven_89);
  not not_8 (not_8_out, undriven_90);
  not not_9 (not_9_out, undriven_91);
  not not_10 (not_10_out, undriven_92);
  not not_11 (not_11_out, undriven_93);
  not not_12 (not_12_out, undriven_94);
  not not_13 (not_13_out, undriven_95);
  not not_14 (not_14_out, undriven_96);
  not not_15 (not_15_out, undriven_97);
  not not_16 (not_16_out, undriven_98);
  not not_17 (not_17_out, undriven_99);
  not not_18 (not_18_out, undriven_100);
  not not_19 (not_19_out, undriven_101);
  not not_20 (not_20_out, undriven_102);
  not not_21 (not_21_out, undriven_103);
  or or_20 (or_20_out, undriven_104, undriven_105);
  or or_21 (or_21_out, undriven_106, undriven_107);
  or or_22 (or_22_out, undriven_108, undriven_109);
  or or_23 (or_23_out, undriven_110, undriven_111);
  Multiplexer multiplexer_2 (.in0(undriven_112), .in1(undriven_113), .out(multiplexer_2_out), .sel(undriven_144));
  Multiplexer multiplexer_3 (.in0(undriven_114), .in1(undriven_115), .out(multiplexer_3_out), .sel(undriven_145));
  Multiplexer multiplexer_4 (.in0(undriven_116), .in1(undriven_117), .out(multiplexer_4_out), .sel(undriven_146));
  Multiplexer multiplexer_5 (.in0(undriven_118), .in1(undriven_119), .out(multiplexer_5_out), .sel(undriven_147));
  Multiplexer multiplexer_6 (.in0(undriven_120), .in1(undriven_121), .out(multiplexer_6_out), .sel(undriven_148));
  Multiplexer multiplexer_7 (.in0(undriven_122), .in1(undriven_123), .out(multiplexer_7_out), .sel(undriven_149));
  Multiplexer multiplexer_8 (.in0(undriven_124), .in1(undriven_125), .out(multiplexer_8_out), .sel(undriven_150));
  Multiplexer multiplexer_9 (.in0(undriven_126), .in1(undriven_127), .out(multiplexer_9_out), .sel(undriven_151));
  Multiplexer multiplexer_10 (.in0(undriven_128), .in1(undriven_129), .out(multiplexer_10_out), .sel(undriven_152));
  Multiplexer multiplexer_11 (.in0(undriven_130), .in1(undriven_131), .out(multiplexer_11_out), .sel(undriven_153));
  Multiplexer multiplexer_12 (.in0(undriven_132), .in1(undriven_133), .out(multiplexer_12_out), .sel(undriven_154));
  Multiplexer multiplexer_13 (.in0(undriven_134), .in1(undriven_135), .out(multiplexer_13_out), .sel(undriven_155));
  Multiplexer multiplexer_14 (.in0(undriven_136), .in1(undriven_137), .out(multiplexer_14_out), .sel(undriven_156));
  Multiplexer multiplexer_15 (.in0(undriven_138), .in1(undriven_139), .out(multiplexer_15_out), .sel(undriven_157));
  Multiplexer multiplexer_16 (.in0(undriven_140), .in1(undriven_141), .out(multiplexer_16_out), .sel(undriven_158));
  Multiplexer multiplexer_17 (.in0(undriven_142), .in1(undriven_143), .out(multiplexer_17_out), .sel(undriven_159));
  or or_24 (or_24_out, or_20_out, or_21_out);
  or or_25 (or_25_out, or_22_out, or_23_out);
  or or_26 (or_26_out, or_24_out, or_25_out);
  Multiplexer #(.width(16)) multiplexer_18 (
    .in0(undriven_168), .in1(undriven_169), .out(multiplexer_18_out), .sel(undriven_174));
  Multiplexer #(.width(16)) multiplexer_19 (
    .in0(undriven_170), .in1(undriven_171), .out(multiplexer_19_out), .sel(undriven_174));
  Multiplexer #(.width(16)) multiplexer_20 (
    .in0(undriven_160), .in1(undriven_161), .out(multiplexer_20_out), .sel(undriven_172));
  Multiplexer #(.width(16)) multiplexer_21 (
    .in0(undriven_162), .in1(undriven_163), .out(multiplexer_21_out), .sel(undriven_172));
  Multiplexer #(.width(16)) multiplexer_22 (
    .in0(undriven_164), .out(multiplexer_22_out), .sel(undriven_172));  // open: in1
  Multiplexer #(.width(16)) multiplexer_23 (
    .in0(undriven_165), .in1(undriven_166), .out(multiplexer_23_out), .sel(undriven_172));
  Demultiplexer demultiplexer_2 (
    .out0(demultiplexer_2_out0), .out1(demultiplexer_2_out1), .in(undriven_173), .sel(undriven_176));
  Demultiplexer demultiplexer_3 (
    .out0(demultiplexer_3_out0), .out1(demultiplexer_3_out1), .in(undriven_167), .sel(undriven_175));
  Multiplexer #(.width(16)) multiplexer_24 (
    .in0(multiplexer_18_out), .in1(multiplexer_19_out), .out(multiplexer_24_out), .sel(undriven_179));
  Multiplexer #(.width(16)) multiplexer_25 (
    .in0(multiplexer_20_out), .in1(multiplexer_21_out), .out(multiplexer_25_out), .sel(undriven_177));
  Multiplexer #(.width(16)) multiplexer_26 (
    .in0(multiplexer_22_out), .in1(multiplexer_23_out), .out(multiplexer_26_out), .sel(undriven_177));
  Demultiplexer demultiplexer_4 (
    .out0(demultiplexer_4_out0), .out1(demultiplexer_4_out1), .in(demultiplexer_2_out0), .sel(undriven_180));
  Demultiplexer demultiplexer_5 (
    .out0(demultiplexer_5_out0), .out1(demultiplexer_5_out1), .in(demultiplexer_2_out1), .sel(undriven_180));
  Demultiplexer demultiplexer_6 (
    .out0(demultiplexer_6_out0), .out1(demultiplexer_6_out1), .in(demultiplexer_3_out0), .sel(undriven_178));
  Demultiplexer demultiplexer_7 (
    .out0(demultiplexer_7_out0), .out1(demultiplexer_7_out1), .in(demultiplexer_3_out1), .sel(undriven_178));
  Multiplexer #(.width(16)) multiplexer_27 (
    .in0(multiplexer_25_out), .in1(multiplexer_26_out), .out(multiplexer_27_out), .sel(undriven_181));
  Demultiplexer demultiplexer_8 (
    .out0(demultiplexer_8_out0), .out1(demultiplexer_8_out1), .in(demultiplexer_6_out0), .sel(undriven_182));
  Demultiplexer demultiplexer_9 (
    .out0(demultiplexer_9_out0), .out1(demultiplexer_9_out1), .in(demultiplexer_6_out1), .sel(undriven_182));
  Demultiplexer demultiplexer_10 (
    .out0(demultiplexer_10_out0), .out1(demultiplexer_10_out1), .in(demultiplexer_7_out0), .sel(undriven_182));
  Demultiplexer demultiplexer_11 (
    .out0(demultiplexer_11_out0), .out1(demultiplexer_11_out1), .in(demultiplexer_7_out1), .sel(undriven_182));

  // Notes on the sheet:
  //   a
  //   b
  //   a
  //   b
  //   a
  //   b
  //   a
  //   b
  //   a
  //   b
  //   a
  //   b
  //   a
  //   b
  //   a
  //   b
  //   a
  //   b
  //   a
  //   b
  //   a
  //   b
  //   a
  //   b
  //   a
  //   b
  //   a
  //   b
  //   a
  //   b
  //   a
  //   b
  //   in
  //   a
  //   b
  //   a
  //   b
  //   a
  //   b
  //   a
  //   b
  //   in
  //   AND16
  //   NOT
  //   AND
  //   OR
  //   XOR
  //   sel
  //   sel
  //   out
  //   out
  //   out
  //   out
  //   out
  //   a
  //   b
  //   b
  //   b
  //   in
  //   in
  //   a
  //   b
  //   a
  //   b
  //   a
  //   b
  //   sel
  //   a
  //   b
  //   a
  //   b
  //   a
  //   b
  //   a
  //   b
  //   a
  //   b
  //   a
  //   b
  //   a
  //   b
  //   a
  //   b
  //   a
  //   b
  //   a
  //   b
  //   a
  //   b
  //   a
  //   b
  //   a
  //   b
  //   a
  //   b
  //   a
  //   b
  //   a
  //   b
  //   sel
  //   OR16
  //   out
  //   out
  //   out
  //   a
  //   b
  //   out
  //   NOT16
  //   OR8WAY16
  //   Mux16
  //   Mux8Way16
  //   sel[0]
  //   MUX4WAY16
  //   sel[0]
  //   sel[1]
  //   sel[2]
  //   sel[1]
  //   sel[1]
  //   sel[1]
  //   sel[2]
  //   sel[0]
  //   sel[0]
  //   sel[0]
endmodule
