// Logisim project gates_diagrams.circ as structural Verilog: 1 circuit, main circuit main
module main (
  input  in_1
);

  wire and_1_out, and_2_out, and_3_out, and_4_out, and_5_out, and_6_out, and_7_out, and_8_out, and_9_out,
       and_10_out, and_11_out, and_12_out, and_13_out, and_14_out, and_15_out, and_16_out, and_17_out,
       and_18_out, and_19_out, and_20_out, and_21_out, and_22_out, and_23_out, buffer_1_out, buffer_2_out,
       demultiplexer_1_out0, demultiplexer_1_out1, demultiplexer_2_out0, demultiplexer_2_out1,
       demultiplexer_3_out0, demultiplexer_3_out1, demultiplexer_4_out0, demultiplexer_4_out1,
       demultiplexer_5_out0, demultiplexer_5_out1, demultiplexer_6_out0, demultiplexer_6_out1,
       demultiplexer_7_out0, demultiplexer_7_out1, demultiplexer_8_out0, demultiplexer_8_out1,
       demultiplexer_9_out0, demultiplexer_9_out1, demultiplexer_10_out0, demultiplexer_10_out1,
       demultiplexer_11_out0, demultiplexer_11_out1, multiplexer_1_out, multiplexer_2_out, multiplexer_3_out,
       multiplexer_4_out, multiplexer_5_out, multiplexer_6_out, multiplexer_7_out, multiplexer_8_out,
       multiplexer_9_out, multiplexer_10_out, multiplexer_11_out, multiplexer_12_out, multiplexer_13_out,
       multiplexer_14_out, multiplexer_15_out, multiplexer_16_out, multiplexer_17_out, nand_1_out,
       nand_2_out, nand_3_out, nand_4_out, not_1_out, not_2_out, not_3_out, not_4_out, not_5_out, not_6_out,
       not_7_out, not_8_out, not_9_out, not_10_out, not_11_out, not_12_out, not_13_out, not_14_out,
       not_15_out, not_16_out, not_17_out, not_18_out, not_19_out, not_20_out, not_21_out, or_1_out,
       or_2_out, or_3_out, or_4_out, or_5_out, or_6_out, or_7_out, or_8_out, or_9_out, or_10_out, or_11_out,
       or_12_out, or_13_out, or_14_out, or_15_out, or_16_out, or_17_out, or_18_out, or_19_out, or_20_out,
       or_21_out, or_22_out, or_23_out, or_24_out, or_25_out, or_26_out, undriven, undriven_2, undriven_3,
       undriven_4, undriven_5, undriven_6, undriven_7, undriven_8, undriven_9, undriven_10, undriven_11,
       undriven_12, undriven_13, undriven_14, undriven_15, undriven_16, undriven_17, undriven_18,
       undriven_19, undriven_20, undriven_21, undriven_22, undriven_23, undriven_24, undriven_25,
       undriven_26, undriven_27, undriven_28, undriven_29, undriven_30, undriven_31, undriven_32,
       undriven_33, undriven_34, undriven_35, undriven_36, undriven_37, undriven_38, undriven_39,
       undriven_40, undriven_41, undriven_42, undriven_43, undriven_44, undriven_45, undriven_46,
       undriven_47, undriven_48, undriven_49, undriven_50, undriven_51, undriven_52, undriven_53,
       undriven_54, undriven_55, undriven_56, undriven_57, undriven_58, undriven_59, undriven_60,
       undriven_61, undriven_62, undriven_63, undriven_64, undriven_65, undriven_66, undriven_67,
       undriven_68, undriven_69, undriven_70, undriven_71, undriven_72, undriven_73, undriven_74,
       undriven_75, undriven_76, undriven_77, undriven_78, undriven_79, undriven_80, undriven_81,
       undriven_82, undriven_83, undriven_84, undriven_85, undriven_86, undriven_87, undriven_88,
       undriven_89, undriven_90, undriven_91, undriven_92, undriven_93, undriven_94, undriven_95,
       undriven_96, undriven_97, undriven_98, undriven_99, undriven_100, undriven_101, undriven_102,
       undriven_103, undriven_104, undriven_105, undriven_106, undriven_107, undriven_108, undriven_109,
       undriven_110, undriven_111, undriven_119, undriven_124, undriven_125, undriven_126, undriven_127,
       undriven_128, undriven_129, undriven_130, undriven_131, undriven_132, undriven_133, undriven_134,
       undriven_135, undriven_136, undriven_137, undriven_138, undriven_139, undriven_140, undriven_141,
       undriven_142, undriven_143, undriven_144, undriven_145, undriven_146, undriven_147, undriven_148,
       undriven_149, undriven_150, undriven_151, undriven_152, xor_1_out;
  wire [15:0] multiplexer_18_out, multiplexer_19_out, multiplexer_20_out, multiplexer_21_out,
       multiplexer_22_out, multiplexer_23_out, multiplexer_24_out, multiplexer_25_out, multiplexer_26_out,
       multiplexer_27_out, undriven_112, undriven_113, undriven_114, undriven_115, undriven_116,
       undriven_117, undriven_118, undriven_120, undriven_121, undriven_122, undriven_123;

  and and_1 (and_1_out, undriven, undriven_2);
  or or_1 (or_1_out, undriven_3, undriven_4);
  not not_1 (not_1_out, undriven_5);
  not not_2 (not_2_out, undriven_6);
  not not_3 (not_3_out, undriven_7);
  not not_4 (not_4_out, undriven_8);
  not not_5 (not_5_out, undriven_9);
  not not_6 (not_6_out, undriven_10);
  not not_7 (not_7_out, undriven_11);
  not not_8 (not_8_out, undriven_12);
  not not_9 (not_9_out, undriven_13);
  not not_10 (not_10_out, undriven_14);
  not not_11 (not_11_out, undriven_15);
  not not_12 (not_12_out, undriven_16);
  not not_13 (not_13_out, undriven_17);
  not not_14 (not_14_out, undriven_18);
  not not_15 (not_15_out, undriven_19);
  not not_16 (not_16_out, undriven_20);
  or or_2 (or_2_out, undriven_21, undriven_22);
  or or_3 (or_3_out, undriven_23, undriven_24);
  or or_4 (or_4_out, undriven_25, undriven_26);
  or or_5 (or_5_out, undriven_27, undriven_28);
  Multiplexer multiplexer_1 (.in0(undriven_29), .in1(undriven_30), .out(multiplexer_1_out), .sel(undriven_61));
  Multiplexer multiplexer_2 (.in0(undriven_31), .in1(undriven_32), .out(multiplexer_2_out), .sel(undriven_62));
  Multiplexer multiplexer_3 (.in0(undriven_33), .in1(undriven_34), .out(multiplexer_3_out), .sel(undriven_63));
  Multiplexer multiplexer_4 (.in0(undriven_35), .in1(undriven_36), .out(multiplexer_4_out), .sel(undriven_64));
  Multiplexer multiplexer_5 (.in0(undriven_37), .in1(undriven_38), .out(multiplexer_5_out), .sel(undriven_65));
  Multiplexer multiplexer_6 (.in0(undriven_39), .in1(undriven_40), .out(multiplexer_6_out), .sel(undriven_66));
  Multiplexer multiplexer_7 (.in0(undriven_41), .in1(undriven_42), .out(multiplexer_7_out), .sel(undriven_67));
  Multiplexer multiplexer_8 (.in0(undriven_43), .in1(undriven_44), .out(multiplexer_8_out), .sel(undriven_68));
  Multiplexer multiplexer_9 (.in0(undriven_45), .in1(undriven_46), .out(multiplexer_9_out), .sel(undriven_69));
  Multiplexer multiplexer_10 (.in0(undriven_47), .in1(undriven_48), .out(multiplexer_10_out), .sel(undriven_70));
  Multiplexer multiplexer_11 (.in0(undriven_49), .in1(undriven_50), .out(multiplexer_11_out), .sel(undriven_71));
  Multiplexer multiplexer_12 (.in0(undriven_51), .in1(undriven_52), .out(multiplexer_12_out), .sel(undriven_72));
  Multiplexer multiplexer_13 (.in0(undriven_53), .in1(undriven_54), .out(multiplexer_13_out), .sel(undriven_73));
  Multiplexer multiplexer_14 (.in0(undriven_55), .in1(undriven_56), .out(multiplexer_14_out), .sel(undriven_74));
  Multiplexer multiplexer_15 (.in0(undriven_57), .in1(undriven_58), .out(multiplexer_15_out), .sel(undriven_75));
  Multiplexer multiplexer_16 (.in0(undriven_59), .in1(undriven_60), .out(multiplexer_16_out), .sel(undriven_76));
  and and_2 (and_2_out, and_1_out, undriven_77);
  or or_6 (or_6_out, or_1_out, undriven_78);
  or or_7 (or_7_out, or_2_out, or_3_out);
  or or_8 (or_8_out, or_4_out, or_5_out);
  not not_17 (not_17_out, undriven_81);
  and and_3 (and_3_out, undriven_82, undriven_83);
  or or_9 (or_9_out, undriven_84, undriven_85);
  Multiplexer multiplexer_17 (.in0(undriven_88), .in1(undriven_89), .out(multiplexer_17_out), .sel(undriven_91));
  Demultiplexer demultiplexer_1 (
    .out0(demultiplexer_1_out0), .out1(demultiplexer_1_out1), .in(undriven_90));  // open: sel
  and and_4 (and_4_out, and_2_out, undriven_79);
  or or_10 (or_10_out, or_6_out, undriven_80);
  or or_11 (or_11_out, or_7_out, or_8_out);
  xor xor_1 (xor_1_out, undriven_86, undriven_87);
  and and_5 (and_5_out, and_4_out, undriven_92);
  or or_12 (or_12_out, or_10_out, undriven_93);
  and and_6 (and_6_out, and_5_out, undriven_95);
  or or_13 (or_13_out, or_12_out, undriven_94);
  nand nand_1 (nand_1_out, undriven_105, undriven_105);
  nand nand_2 (nand_2_out, undriven_99, undriven_100);
  buf buffer_1 (buffer_1_out, undriven_101);
  buf buffer_2 (buffer_2_out, undriven_102);
  not not_18 (not_18_out, undriven_96);
  not not_19 (not_19_out, undriven_97);
  not not_20 (not_20_out, undriven_107);
  not not_21 (not_21_out, undriven_106);
  or or_14 (or_14_out, or_13_out, undriven_108);
  nand nand_3 (nand_3_out, buffer_1_out, buffer_2_out);
  and and_7 (and_7_out, not_18_out, undriven_97);
  and and_8 (and_8_out, undriven_96, not_19_out);
  and and_9 (and_9_out, undriven_103, not_20_out);
  and and_10 (and_10_out, undriven_104, undriven_107);
  and and_11 (and_11_out, not_21_out, undriven_98);
  and and_12 (and_12_out, undriven_106, undriven_98);
  and and_13 (and_13_out, and_6_out, undriven_109);
  Multiplexer #(.width(16)) multiplexer_18 (
    .in0(undriven_112), .in1(undriven_113), .out(multiplexer_18_out), .sel(undriven_124));
  Multiplexer #(.width(16)) multiplexer_19 (
    .in0(undriven_114), .in1(undriven_115), .out(multiplexer_19_out), .sel(undriven_124));
  Multiplexer #(.width(16)) multiplexer_20 (
    .in0(undriven_116), .out(multiplexer_20_out), .sel(undriven_124));  // open: in1
  Multiplexer #(.width(16)) multiplexer_21 (
    .in0(undriven_117), .in1(undriven_118), .out(multiplexer_21_out), .sel(undriven_124));
  Demultiplexer demultiplexer_2 (
    .out0(demultiplexer_2_out0), .out1(demultiplexer_2_out1), .in(undriven_125), .sel(undriven_128));
  Demultiplexer demultiplexer_3 (
    .out0(demultiplexer_3_out0), .out1(demultiplexer_3_out1), .in(undriven_119), .sel(undriven_127));
  nand nand_4 (nand_4_out, nand_2_out, nand_2_out);
  or or_15 (or_15_out, and_7_out, and_8_out);
  or or_16 (or_16_out, and_9_out, and_10_out);
  and and_14 (and_14_out, and_13_out, undriven_111);
  or or_17 (or_17_out, or_14_out, undriven_110);
  Multiplexer #(.width(16)) multiplexer_22 (
    .in0(undriven_120), .in1(undriven_121), .out(multiplexer_22_out), .sel(undriven_126));
  Multiplexer #(.width(16)) multiplexer_23 (
    .in0(undriven_122), .in1(undriven_123), .out(multiplexer_23_out), .sel(undriven_126));
  Multiplexer #(.width(16)) multiplexer_24 (
    .in0(multiplexer_18_out), .in1(multiplexer_19_out), .out(multiplexer_24_out), .sel(undriven_131));
  Multiplexer #(.width(16)) multiplexer_25 (
    .in0(multiplexer_20_out), .in1(multiplexer_21_out), .out(multiplexer_25_out), .sel(undriven_131));
  Demultiplexer demultiplexer_4 (
    .out0(demultiplexer_4_out0), .out1(demultiplexer_4_out1), .in(demultiplexer_3_out0), .sel(undriven_132));
  Demultiplexer demultiplexer_5 (
    .out0(demultiplexer_5_out0), .out1(demultiplexer_5_out1), .in(demultiplexer_3_out1), .sel(undriven_132));
  and and_15 (and_15_out, and_14_out, undriven_130);
  or or_18 (or_18_out, or_17_out, undriven_129);
  Multiplexer #(.width(16)) multiplexer_26 (
    .in0(multiplexer_22_out), .in1(multiplexer_23_out), .out(multiplexer_26_out), .sel(undriven_133));
  Multiplexer #(.width(16)) multiplexer_27 (
    .in0(multiplexer_24_out), .in1(multiplexer_25_out), .out(multiplexer_27_out), .sel(undriven_137));
  Demultiplexer demultiplexer_6 (
    .out0(demultiplexer_6_out0), .out1(demultiplexer_6_out1), .in(demultiplexer_2_out0), .sel(undriven_134));
  Demultiplexer demultiplexer_7 (
    .out0(demultiplexer_7_out0), .out1(demultiplexer_7_out1), .in(demultiplexer_2_out1), .sel(undriven_134));
  Demultiplexer demultiplexer_8 (
    .out0(demultiplexer_8_out0), .out1(demultiplexer_8_out1), .in(demultiplexer_4_out0), .sel(undriven_138));
  Demultiplexer demultiplexer_9 (
    .out0(demultiplexer_9_out0), .out1(demultiplexer_9_out1), .in(demultiplexer_4_out1), .sel(undriven_138));
  Demultiplexer demultiplexer_10 (
    .out0(demultiplexer_10_out0), .out1(demultiplexer_10_out1), .in(demultiplexer_5_out0), .sel(undriven_138));
  Demultiplexer demultiplexer_11 (
    .out0(demultiplexer_11_out0), .out1(demultiplexer_11_out1), .in(demultiplexer_5_out1), .sel(undriven_138));
  and and_16 (and_16_out, and_15_out, undriven_136);
  or or_19 (or_19_out, or_18_out, undriven_135);
  and and_17 (and_17_out, and_16_out, undriven_140);
  or or_20 (or_20_out, or_19_out, undriven_139);
  and and_18 (and_18_out, and_17_out, undriven_142);
  or or_21 (or_21_out, or_20_out, undriven_141);
  and and_19 (and_19_out, and_18_out, undriven_144);
  or or_22 (or_22_out, or_21_out, undriven_143);
  or or_23 (or_23_out, or_22_out, undriven_145);
  and and_20 (and_20_out, and_19_out, undriven_146);
  or or_24 (or_24_out, or_23_out, undriven_147);
  and and_21 (and_21_out, and_20_out, undriven_148);
  and and_22 (and_22_out, and_21_out, undriven_150);
  or or_25 (or_25_out, or_24_out, undriven_149);
  and and_23 (and_23_out, and_22_out, undriven_152);
  or or_26 (or_26_out, or_25_out, undriven_151);

  // Notes on the sheet:
  //   AND16
  //   a
  //   a
  //   a
  //   b
  //   b
  //   b
  //   OR16
  //   a
  //   b
  //   NOT16
  //   OR8WAY16
  //   Mux16
  //   in
  //   a
  //   b
  //   a
  //   b
  //   a
  //   b
  //   a
  //   b
  //   in
  //   NOT
  //   AND
  //   OR
  //   XOR
  //   sel
  //   sel
  //   out
  //   out
  //   out
  //   out
  //   out
  //   a
  //   b
  //   b
  //   b
  //   in
  //   in
  //   a
  //   b
  //   a
  //   b
  //   a
  //   b
  //   sel
  //   sel
  //   out
  //   sel[0]
  //   Mux8Way16
  //   sel[0]
  //   sel[2]
  //   out
  //   out
  //   a
  //   b
  //   MUX4WAY16
  //   sel[1]
  //   sel[1]
  //   sel[1]
  //   out
  //   sel[2]
  //   sel[0]
  //   sel[1]
  //   sel[0]
  //   out
  //   sel[0]
endmodule
